// Logisim project coconut16.circ as structural Verilog: 3 circuits, main circuit main
module main (
  input  [15:0] in_1,
  input  [7:0] in_2,
  input  in_3,
  input  in_4,
  input  in_5,
  input  in_6,
  input  [15:0] in_7,
  input  in_8,
  input  [11:0] in_9,
  input  [11:0] in_10,
  input  [11:0] in_11,
  output out_12,
  output [15:0] out_13
);

  wire cdm16_1_p1, cdm16_1_p2, clock_1_out, clock_2_out, dma_1_device_rd_wr_prime, dma_1_ram_rd_wr_prime;
  wire [1:0] mmu_1_exception_number;
  wire [11:0] bit_extender_2_out;
  wire [15:0] buffer_2_out, buffer_4_out, cdm16_1_p3, cdm16_1_p4, cdm16_1_p5, dma_1_bus_data_out,
       dma_1_device_data_out;
  wire [19:0] dma_1_ram_address, mmu_1_physical_address;
  wire [23:0] bit_extender_1_out;
  wire [31:0] dma_1_device_address;

  // cdm16 cdm16_1: pin names not known; wires that end beside it: cdm16_1_p1, cdm16_1_p2, cdm16_1_p3, cdm16_1_p4, cdm16_1_p5
  assign cdm16_1_p5 = buffer_2_out;  // Buffer buffer_1, 16 bits wide
  assign buffer_2_out = cdm16_1_p4;  // Buffer buffer_2, 16 bits wide
  Bit_Extender #(.in_width(32), .out_width(24)) bit_extender_1 (.in(dma_1_device_address), .out(bit_extender_1_out));
  Bit_Extender #(.in_width(16), .out_width(12)) bit_extender_2 (.in(cdm16_1_p3), .out(bit_extender_2_out));
  assign buffer_2_out = dma_1_bus_data_out;  // Buffer buffer_3, 16 bits wide
  assign buffer_4_out = buffer_2_out;  // Buffer buffer_4, 16 bits wide
  DMA dma_1 (
    .mem(cdm16_1_p2), .io(in_8), .iack(cdm16_1_p1), .device_data_in(dma_1_device_data_out),
    .bus_data_in(buffer_4_out), .Address(bit_extender_2_out), .RAM_register_addr(in_9),
    .Sector_no_reg_addr(in_10), .Control_reg_addr(in_11), .Clock(clock_1_out),
    .RAM_rd_wr_prime(dma_1_ram_rd_wr_prime), .Device_rd_wr_prime(dma_1_device_rd_wr_prime),
    .Device_address(dma_1_device_address), .device_data_out(dma_1_device_data_out),
    .bus_data_out(dma_1_bus_data_out), .RAM_address(dma_1_ram_address));  // open: IRQ, mem_2
  Clock clock_1 (.out(clock_1_out));
  RAM #(.addrWidth(24), .dataWidth(16)) ram_1 (
    .addr(bit_extender_1_out), .data(dma_1_device_data_out), .clk(clock_1_out), .ld(dma_1_device_rd_wr_prime));  // open: sel, clr
  D_Flip_Flop d_ff_1 ();  // open: clk, D, Q, Qn, preset, en, reset
  MMU mmu_1 (
    .Virtual_address(in_1), .Context_number(in_2), .Data(in_3), .Clock__generator(clock_2_out),
    .Physical_address(mmu_1_physical_address), .Exception(out_12), .Vector(in_5), .IO_enable(in_4),
    .Data_In(in_7), .Data_out(out_13), .Context_register_address({12{1'b0}}), .Table_address(12'h80),
    .rd_wr_prime(in_6), .Exception_number(mmu_1_exception_number));  // open: Exception_address_register
  Clock clock_2 (.out(clock_2_out));
  // Probe on mmu_1_physical_address
  // Probe on mmu_1_exception_number
  RAM #(.addrWidth(20), .dataWidth(16)) ram_2 (
    .addr(dma_1_ram_address), .data(buffer_2_out), .clk(dma_1_ram_rd_wr_prime), .ld(clock_1_out));  // open: sel, clr
endmodule

module MMU (
  input  IO_enable,
  input  Vector,
  input  rd_wr_prime,
  input  [15:0] Data_In,
  input  [15:0] Virtual_address,
  input  [7:0] Context_number,
  input  Data,
  input  Clock__generator,
  input  [11:0] Context_register_address,
  input  [11:0] Exception_address_register,
  input  [11:0] Table_address,
  output [19:0] Physical_address,
  output [1:0] Exception_number,
  output Exception,
  output [15:0] Data_out
);

  wire and_5_out, and_6_out, and_7_out, comparator_1_eq, comparator_2_eq, comparator_3_gt, comparator_4_lt,
       comparator_6_lt, comparator_7_lt, Context_register_select, Device_area, Exception_register_select,
       Flags_table_select, Inverse_bit, multiplexer_2_out, not_1_out, not_2_out, not_3_out, not_4_out,
       not_5_out, not_6_out, not_7_out, or_1_out, Paragraph_offset_select, Presence_bit,
       pull_resistor_1_node, Table_select, Translation, Use_constants;
  wire [1:0] priority_encoder_1_out, priority_encoder_2_out;
  wire [1:1] Segment_flags;
  wire [7:0] Context_register, multiplexer_1_out;
  wire [11:0] adder_1_out, subtractor_1_out;
  wire [12:0] multiplexer_5_out, multiplexer_6_out, Segment_info;
  wire [15:0] bit_extender_2_out, Exception_address, Paragraph_offset;
  wire [19:0] adder_2_out, bit_extender_1_out, Device_area_Address, subtractor_2_out, Vector_Address;

  Adder #(.width(12)) adder_1 (.a(Table_address), .b(12'h80), .out(adder_1_out));  // open: cin, cout
  Comparator #(.width(12), .mode("unsigned")) comparator_1 (
    .a(Virtual_address[11:0]), .b(Context_register_address), .eq(comparator_1_eq));  // open: gt, lt
  Comparator #(.width(12), .mode("unsigned")) comparator_2 (
    .a(Virtual_address[11:0]), .b(Exception_address_register), .eq(comparator_2_eq));  // open: gt, lt
  Register register_1 (
    .D(Data_In[7:0]), .en(Context_register_select), .Q(Context_register), .clk(Clock__generator));  // open: clr
  and and_1 (Context_register_select, Device_area, comparator_1_eq);
  and and_2 (Exception_register_select, Device_area, comparator_2_eq);
  not not_1 (not_1_out, comparator_3_gt);
  Comparator #(.width(12), .mode("unsigned")) comparator_3 (
    .a(Table_address), .b(Virtual_address[11:0]), .gt(comparator_3_gt));  // open: eq, lt
  Comparator #(.width(12), .mode("unsigned")) comparator_4 (
    .a(Virtual_address[11:0]), .b(adder_1_out), .lt(comparator_4_lt));  // open: gt, eq
  and and_3 (Table_select, not_1_out, comparator_4_lt, Device_area);
  Demultiplexer #(.disabled(0)) demultiplexer_1 (
    .out0(Flags_table_select), .out1(Paragraph_offset_select), .in(Table_select), .sel(not_2_out),
    .en(Virtual_address[6]));
  not not_2 (not_2_out, rd_wr_prime);
  Multiplexer #(.width(8), .enable("false")) multiplexer_1 (
    .in0(Context_number), .in1(Context_register), .out(multiplexer_1_out), .sel(Device_area));
  Comparator comparator_5 (.a(multiplexer_1_out), .b({8{1'b0}}), .eq(Use_constants));  // open: gt, lt
  assign bit_extender_1_out = {{8{1'b0}}, Virtual_address[11:0]};  // Bit_Extender bit_extender_1
  not not_3 (not_3_out, Use_constants);
  Comparator #(.width(12), .mode("unsigned")) comparator_6 (
    .a(Virtual_address[11:0]), .b({Segment_info[7:0], 4'b0000}), .lt(comparator_6_lt));  // open: gt, eq
  ROM #(.addrWidth(5), .dataWidth(32)) rom_1 (
    .addr({Data, Virtual_address[15:12]}),
    .data({Paragraph_offset, Presence_bit, Segment_flags[1], Inverse_bit, Segment_info}), .sel(Use_constants));
  Adder #(.width(20)) adder_2 (
    .a({Paragraph_offset, 4'b0000}), .b(bit_extender_1_out), .out(adder_2_out));  // open: cin, cout
  Pull_Resistor pull_resistor_1 (.node(pull_resistor_1_node));
  assign pull_resistor_1_node = not_3_out ? Vector : 1'bz;  // Controlled_Buffer controlled_buffer_1
  not not_4 (not_4_out, comparator_6_lt);
  Subtractor #(.width(12)) subtractor_1 (
    .a({12{1'b1}}), .b({Segment_info[7:0], 4'b0000}), .out(subtractor_1_out));  // open: bin, bout
  Comparator #(.width(12), .mode("unsigned")) comparator_7 (
    .a(subtractor_1_out), .b(Virtual_address[11:0]), .lt(comparator_7_lt));  // open: gt, eq
  and and_4 (Device_area, Virtual_address[12], Virtual_address[13], Virtual_address[14], Virtual_address[15], Data, IO_enable);
  Subtractor #(.width(20)) subtractor_2 (.a(adder_2_out), .b(20'h1000), .out(subtractor_2_out));  // open: bin, bout
  Multiplexer #(.enable("false")) multiplexer_2 (
    .in0(not_4_out), .in1(not_5_out), .out(multiplexer_2_out), .sel(Inverse_bit));
  not not_5 (not_5_out, comparator_7_lt);
  assign bit_extender_2_out = {{8{1'b0}}, Context_register};  // Bit_Extender bit_extender_2
  Priority_Encoder #(.select(2)) priority_encoder_1 (
    .in0(1'b1), .in1(Virtual_address[6]), .in2(Context_register_select), .in3(Exception_register_select),
    .out(priority_encoder_1_out));  // open: gs, en_out, en_in
  Multiplexer #(.select(2), .width(20), .enable("false")) multiplexer_3 (
    .in0(adder_2_out), .in1(subtractor_2_out), .in2(Vector_Address), .in3(Device_area_Address),
    .out(Physical_address), .sel(priority_encoder_2_out));
  Priority_Encoder #(.select(2)) priority_encoder_2 (
    .in0(1'b1), .in1(Inverse_bit), .in2(pull_resistor_1_node), .in3(Device_area), .out(priority_encoder_2_out));  // open: gs, en_out, en_in
  and and_5 (and_5_out, rd_wr_prime, or_1_out);
  or or_1 (or_1_out, Context_register_select, Exception_register_select, Table_select);
  and and_6 (and_6_out, Segment_flags[1], Translation, ~rd_wr_prime);  // AND_Gate
  and and_7 (and_7_out, Translation, ~Presence_bit);  // AND_Gate
  Multiplexer #(.select(2), .width(16)) multiplexer_4 (
    .in0({Presence_bit, Segment_flags[1], Inverse_bit, Segment_info}), .in1(Paragraph_offset),
    .in2(bit_extender_2_out), .in3(Exception_address), .out(Data_out), .sel(priority_encoder_1_out),
    .en(and_5_out));
  Register #(.width(16), .trigger("falling")) register_2 (
    .D(Virtual_address), .en(Exception), .Q(Exception_address), .clk(Clock__generator));  // open: clr
  Priority_Encoder #(.select(2)) priority_encoder_3 (
    .in1(and_6_out), .in2(multiplexer_2_out), .in3(and_7_out), .out(Exception_number), .gs(Exception),
    .en_in(Translation));  // open: in0, en_out
  Multiplexer #(.width(13), .enable("false")) multiplexer_5 (
    .in0({Context_number, Data, Virtual_address[15:12]}), .in1({Context_register, Virtual_address[5:1]}),
    .out(multiplexer_5_out), .sel(Device_area));
  not not_6 (not_6_out, Use_constants);
  Multiplexer #(.width(13), .enable("false")) multiplexer_6 (
    .in0({Context_number, Data, Virtual_address[15:12]}), .in1({Context_register, Virtual_address[5:1]}),
    .out(multiplexer_6_out), .sel(Device_area));
  not not_7 (not_7_out, Use_constants);
  assign Vector_Address = {{4{1'b0}}, Virtual_address};  // Bit_Extender bit_extender_3
  assign Device_area_Address = {{4{1'b1}}, Virtual_address};  // Bit_Extender bit_extender_4
  Pull_Resistor pull_resistor_2 (.node({Presence_bit, Segment_flags[1], Inverse_bit, Segment_info}));
  RAM #(.addrWidth(13), .dataWidth(16), .bus("separate")) ram_1 (
    .addr(multiplexer_5_out), .din(Data_In),
    .data({Presence_bit, Segment_flags[1], Inverse_bit, Segment_info}), .str(Flags_table_select),
    .sel(not_6_out), .clk(Clock__generator), .ld(1'b1));  // open: clr
  RAM #(.addrWidth(13), .dataWidth(16), .bus("separate")) ram_2 (
    .addr(multiplexer_6_out), .din(Data_In), .data(Paragraph_offset), .str(Paragraph_offset_select),
    .sel(not_7_out), .clk(Clock__generator), .ld(1'b1));  // open: clr
  nor nor_1 (Translation, Device_area, Vector);

  // Other names for the same wires on the sheet: Segment_length[7:0] = Segment_info[7:0];
  //   Segment_flags (some bits) = {Presence_bit, Inverse_bit};
  //   Segment_info[15:13] = {Presence_bit, Segment_flags[1], Inverse_bit}; Write_protect_bit = Segment_flags[1];
  //   Clock = Clock__generator; Descriptor_number[12:0] = {Context_number, Data, Virtual_address[15:12]};
  //   Inner_Des_Num[4:0] = {Data, Virtual_address[15:12]}; Segment_number[3:0] = Virtual_address[15:12];
  //   Device_mode_desriptor_number[12:0] = {Context_register, Virtual_address[5:1]};
  //   Inner_offset[11:0] = Virtual_address[11:0]

  // Notes on the sheet:
  //   Inputs
  //   Translation Inputs
  //   Number that processor wants to write
  //   Updates translation table when toggled
  //   from 0 to 1 in read/write mode
  //   or write protect bit and write wr'
  //   Inverse bit changes check for length
  //   Exceptions, if presence_bit == 0 and any access in translation mode
  //   Context
  //   Translation
  //   mode
  //   Outputs
  //   If zero context: map to ROM
  //   Paragraph length = 16
  //   contents of rom_1 (hex, n*v repeats v):
  //   fa008001
  //   Physical address getter
  //   Segment length and flags getter
  //   Paragraph offset getter
  //   If vector
  //   If device area
endmodule

module DMA (
  input  mem,
  input  io,
  input  iack,
  input  [15:0] device_data_in,
  input  [15:0] bus_data_in,
  input  [11:0] Address,
  input  [11:0] RAM_register_addr,
  input  [11:0] Sector_no_reg_addr,
  input  [11:0] Control_reg_addr,
  input  Clock,
  output mem_2,
  output RAM_rd_wr_prime,
  output Device_rd_wr_prime,
  output [31:0] Device_address,
  output [15:0] device_data_out,
  output [15:0] bus_data_out,
  output [19:0] RAM_address,
  output IRQ
);

  wire _1_sector, _2_sector, Clock_t, comparator_1_eq, comparator_2_eq, comparator_3_eq, comparator_4_eq,
       Control_register_t, End, not_1_out, not_2_out, not_4_out, not_5_out, or_1_out, RAM_address_t;
  wire [8:0] Counter;
  wire [11:0] adder_1_out;
  wire [15:0] Control_register, multiplexer_1_out, RAM_paragraph;
  wire [19:0] bit_extender_1_out, bit_extender_3_out, shifter_2_out;
  wire [31:0] bit_extender_2_out, Sector_no, shifter_1_out;

  not not_1 (not_1_out, mem);
  assign Clock_t = not_1_out ? Clock : 1'bz;  // Controlled_Buffer controlled_buffer_1
  Pull_Resistor pull_resistor_1 (.node(Clock_t));
  Comparator #(.width(12)) comparator_1 (.a(Address), .b(RAM_register_addr), .eq(comparator_1_eq));  // open: gt, lt
  Adder #(.width(12)) adder_1 (.a(12'h1), .b(Sector_no_reg_addr), .out(adder_1_out));  // open: cin, cout
  Comparator #(.width(12)) comparator_2 (.a(Sector_no_reg_addr), .b(Address), .eq(comparator_2_eq));  // open: gt, lt
  Comparator #(.width(12)) comparator_3 (.a(Address), .b(Control_reg_addr), .eq(comparator_3_eq));  // open: gt, lt
  and and_1 (RAM_address_t, io, comparator_1_eq);
  and and_2 (_2_sector, io, comparator_4_eq);
  Comparator #(.width(12)) comparator_4 (.a(Address), .b(adder_1_out), .eq(comparator_4_eq));  // open: gt, lt
  and and_3 (_1_sector, io, comparator_2_eq);
  and and_4 (Control_register_t, io, comparator_3_eq);
  Register #(.width(16)) _1st (.D(bus_data_in), .en(_1_sector), .Q(Sector_no[15:0]), .clk(Clock_t));  // open: clr
  Register #(.width(16)) _2nd (.D(bus_data_in), .en(_2_sector), .Q(Sector_no[31:16]), .clk(Clock_t));  // open: clr
  Register #(.width(16)) ram_address_paragraph (
    .D(bus_data_in), .en(RAM_address_t), .Q(RAM_paragraph), .clk(Clock_t));  // open: clr
  Multiplexer #(.width(16)) multiplexer_1 (
    .in0(bus_data_in), .in1({Control_register[15:3], Device_rd_wr_prime, Control_register[1], 1'b0}),
    .out(multiplexer_1_out), .sel(End));  // open: en
  assign bit_extender_1_out = {{4{1'b0}}, RAM_paragraph};  // Bit_Extender bit_extender_1
  Register #(.width(16), .trigger("falling")) u_Control_register (
    .D(multiplexer_1_out), .en(or_1_out),
    .Q({Control_register[15:3], Device_rd_wr_prime, Control_register[1:0]}), .clk(Clock_t));  // open: clr
  or or_1 (or_1_out, End, Control_register_t);
  // Probe on Counter
  Counter #(.width(9), .max('h1ff), .trigger("falling")) counter_1 (
    .count(Control_register[0]), .Q(Counter), .carry(End), .clk(Clock_t));  // open: load, D, clr
  assign bit_extender_2_out = {{23{1'b0}}, Counter};  // Bit_Extender bit_extender_2
  Shifter #(.width(32)) shifter_1 (.in(Sector_no), .\dist (5'b01001), .out(shifter_1_out));
  assign bus_data_out = Device_rd_wr_prime ? device_data_in : 16'bz;  // Controlled_Buffer controlled_buffer_2
  assign bit_extender_3_out = {{11{1'b0}}, Counter};  // Bit_Extender bit_extender_3
  Shifter #(.width(20)) shifter_2 (.in(bit_extender_1_out), .\dist (5'b00100), .out(shifter_2_out));
  not not_2 (not_2_out, mem);
  and and_5 (mem_2, not_2_out, Control_register[0]);
  not not_3 (RAM_rd_wr_prime, Device_rd_wr_prime);
  Adder #(.width(32)) adder_2 (.a(bit_extender_2_out), .b(shifter_1_out), .out(Device_address));  // open: cin, cout
  not not_4 (not_4_out, Device_rd_wr_prime);
  assign device_data_out = not_4_out ? bus_data_in : 16'bz;  // Controlled_Buffer controlled_buffer_3
  Adder #(.width(20)) adder_3 (.a(bit_extender_3_out), .b(shifter_2_out), .out(RAM_address));  // open: cin, cout
  S_R_Flip_Flop s_r_ff_1 (.S(End), .clk(Clock_t), .R(iack), .Q(IRQ), .en(not_5_out));  // open: Qn, preset, reset
  not not_5 (not_5_out, Control_register[1]);

  // Other names for the same wires on the sheet: Inhibit_IRQ = Control_register[1];
  //   Control_register[2] = Device_rd_wr_prime; Device_to_bus = Device_rd_wr_prime; Bus_in[15:0] = bus_data_in;
  //   Running = Control_register[0]; Device_in[15:0] = device_data_in

  // Notes on the sheet:
  //   Constants
  //   Sector number
endmodule
